// Logisim project ALU .circ as structural Verilog: 1 circuit, main circuit main
module main (
  input  [31:0] A,
  input  [2:0] S0S1S2,
  input  [31:0] B,
  output Zero_Bit,
  output [31:0] Alu_Output
);

  wire comparator_1_lt;
  wire [31:0] adder_1_out, and_1_out, bit_extender_1_out, or_1_out, subtractor_1_out;

  assign or_1_out = A | B;  // OR_Gate or_1, 32 bits wide
  Adder #(.width(32)) adder_1 (.a(B), .b(A), .out(adder_1_out));  // open: cin, cout
  assign and_1_out = B & B;  // AND_Gate and_1, 32 bits wide
  Subtractor #(.width(32)) subtractor_1 (.a(B), .b(A), .out(subtractor_1_out));  // open: bin, bout
  Comparator #(.width(32), .mode("unsigned")) comparator_1 (.a(A), .b(B), .lt(comparator_1_lt));  // open: gt, eq
  assign bit_extender_1_out = {{31{1'b0}}, comparator_1_lt};  // Bit_Extender bit_extender_1
  Comparator #(.width(32)) comparator_2 (.a({32{1'b0}}), .b(Alu_Output), .eq(Zero_Bit));  // open: gt, lt
  Multiplexer #(.select(3), .width(32)) multiplexer_1 (
    .in0(and_1_out), .in1(or_1_out), .in2(adder_1_out), .in6(subtractor_1_out), .in7(bit_extender_1_out),
    .out(Alu_Output), .sel(S0S1S2));  // open: in3, in4, in5, en

  // Notes on the sheet:
  //   Inputs
  //   Output
endmodule
