// Logisim project Lab10_q2.circ as structural Verilog: 5 circuits, main circuit main
module main (
);

  wire alu_2_zero_bit, and_1_out, clk, not_1_out, register_12_q;
  wire [1:0] register_17_q;
  wire [2:0] alucontrol_1_alu_control;
  wire [3:0] register_4_q_2, register_11_q;
  wire [4:0] multiplexer_3_out, reg_splitter_1__11_15, reg_splitter_1__16_20, reg_splitter_1__21_25,
       register_7_q, register_8_q, register_15_q, register_18_q;
  wire [5:0] reg_splitter_1__0_5, reg_splitter_1__26_31;
  wire [8:0] alucontrol_1_regwrt;
  wire [8:4] register_4_q;
  wire [15:0] reg_splitter_1__0_15;
  wire [31:0] adder_1_out, alu_1_alu_output, alu_2_alu_output, bit_extender_1_out, multiplexer_1_out,
       multiplexer_2_out, multiplexer_4_out, ram_1_data, ram_2_data, regfile_1_value_0, regfile_1_value_1,
       register_1_q, register_2_q, register_3_q, register_5_q, register_6_q, register_9_q, register_10_q,
       register_13_q, register_14_q, register_16_q, register_19_q, register_20_q, shifter_1_out;

  Clock clock_1 (.out(clk));
  Multiplexer #(.width(32), .enable("false")) multiplexer_1 (
    .in0(alu_1_alu_output), .in1(register_16_q), .out(multiplexer_1_out), .sel(and_1_out));
  Register #(.width(32)) register_1 (.D(multiplexer_1_out), .en(1'b1), .Q(register_1_q), .clk(clk), .clr(1'b0));
  ALU alu_1 (.A(register_1_q), .B(32'h1), .S0S1S2(3'b010), .Alu_Output(alu_1_alu_output));  // open: Zero_Bit
  RAM #(.addrWidth(24), .dataWidth(32)) ram_1 (
    .addr(register_1_q[23:0]), .data(ram_1_data), .sel(1'b1), .clk(clk), .ld(1'b1), .clr(1'b0));
  Register #(.width(32)) register_2 (.D(ram_1_data), .Q(register_2_q), .clk(clk));  // open: en, clr
  Register #(.width(32)) register_3 (.D(alu_1_alu_output), .Q(register_3_q), .clk(clk));  // open: en, clr
  ALUControl alucontrol_1 (
    .OpCode(reg_splitter_1__26_31), .Funct(reg_splitter_1__0_5), .REGWRT(alucontrol_1_regwrt[0]),
    .MEMTOREG(alucontrol_1_regwrt[1]), .MEMWRITE(alucontrol_1_regwrt[2]), .BRANCH(alucontrol_1_regwrt[3]),
    .ALU_Control(alucontrol_1_alu_control), .ALUSRC(alucontrol_1_regwrt[7]), .REGDST(alucontrol_1_regwrt[8]));
  Reg_Splitter reg_splitter_1 (
    .in_1(register_2_q), ._0_5(reg_splitter_1__0_5), ._26_31(reg_splitter_1__26_31),
    ._21_25(reg_splitter_1__21_25), ._16_20(reg_splitter_1__16_20), ._11_15(reg_splitter_1__11_15),
    ._0_15(reg_splitter_1__0_15));  // open: _0_25
  Register #(.width(9)) register_4 (
    .D({alucontrol_1_regwrt[8:7], alucontrol_1_alu_control, alucontrol_1_regwrt[3:0]}),
    .Q({register_4_q, register_4_q_2}), .clk(clk));  // open: en, clr
  assign bit_extender_1_out = {{16{reg_splitter_1__0_15[15]}}, reg_splitter_1__0_15};  // Bit_Extender bit_extender_1
  Register #(.width(32)) register_5 (.D(regfile_1_value_0), .Q(register_5_q), .clk(clk));  // open: en, clr
  RegFile regfile_1 (
    .Read_0(reg_splitter_1__21_25), .Read_1(reg_splitter_1__16_20), .RegWrite(register_17_q[0]),
    .clear(1'b0), .write_value(multiplexer_4_out), .write_addr(register_18_q), .clock(clk),
    .Value_0(regfile_1_value_0), .Value_1(regfile_1_value_1));  // open: v0
  Register #(.width(32)) register_6 (.D(bit_extender_1_out), .Q(register_6_q), .clk(clk));  // open: en, clr
  Register #(.width(5)) register_7 (.D(reg_splitter_1__11_15), .Q(register_7_q), .clk(clk), .clr(clk));  // open: en
  Register #(.width(5)) register_8 (.D(reg_splitter_1__16_20), .Q(register_8_q), .clk(clk));  // open: en, clr
  Register #(.width(32)) register_9 (.D(register_3_q), .Q(register_9_q), .clk(clk));  // open: en, clr
  Register #(.width(32)) register_10 (.D(regfile_1_value_1), .Q(register_10_q), .clk(clk));  // open: en, clr
  Multiplexer #(.width(32), .enable("false")) multiplexer_2 (
    .in0(register_10_q), .in1(register_6_q), .out(multiplexer_2_out), .sel(register_4_q[7]));
  Shifter #(.width(32)) shifter_1 (.in(register_6_q), .\dist (5'b00010), .out(shifter_1_out));
  ALU alu_2 (
    .A(register_5_q), .B(multiplexer_2_out), .S0S1S2(register_4_q[6:4]), .Zero_Bit(alu_2_zero_bit),
    .Alu_Output(alu_2_alu_output));
  Multiplexer #(.width(5), .disabled(0), .enable("false")) multiplexer_3 (
    .in0(register_7_q), .in1(register_8_q), .out(multiplexer_3_out), .sel(register_4_q[8]));
  Adder #(.width(32)) adder_1 (.a(shifter_1_out), .b(register_9_q), .out(adder_1_out));  // open: cin, cout
  Register #(.width(4)) register_11 (.D(register_4_q_2), .Q(register_11_q), .clk(clk));  // open: en, clr
  Register #(.width(1)) register_12 (.D(alu_2_zero_bit), .Q(register_12_q), .clk(clk));  // open: en, clr
  Register #(.width(32)) register_13 (.D(alu_2_alu_output), .Q(register_13_q), .clk(clk));  // open: en, clr
  Register #(.width(32)) register_14 (.D(register_10_q), .Q(register_14_q), .clk(clk));  // open: en, clr
  Register #(.width(5)) register_15 (.D(multiplexer_3_out), .Q(register_15_q), .clk(clk));  // open: en, clr
  Register #(.width(32)) register_16 (.D(adder_1_out), .Q(register_16_q), .clk(clk));  // open: en, clr
  and and_1 (and_1_out, register_11_q[3], register_12_q);
  not not_1 (not_1_out, register_11_q[2]);
  Register #(.width(2)) register_17 (.D(register_11_q[1:0]), .Q(register_17_q), .clk(clk));  // open: en, clr
  RAM #(.addrWidth(24), .dataWidth(32), .bus("separate")) ram_2 (
    .addr(register_13_q[23:0]), .din(register_14_q), .data(ram_2_data), .str(register_11_q[2]), .sel(1'b1),
    .clk(clk), .ld(not_1_out), .clr(1'b0));
  Register #(.width(5)) register_18 (.D(register_15_q), .Q(register_18_q), .clk(clk));  // open: en, clr
  Register #(.width(32)) register_19 (.D(register_13_q), .Q(register_19_q), .clk(clk));  // open: en, clr
  Register #(.width(32)) register_20 (.D(ram_2_data), .Q(register_20_q), .clk(clk));  // open: en, clr
  Multiplexer #(.width(32), .enable("false")) multiplexer_4 (
    .in0(register_19_q), .in1(register_20_q), .out(multiplexer_4_out), .sel(register_17_q[1]));
endmodule

module ALU (
  input  [31:0] A,
  input  [2:0] S0S1S2,
  input  [31:0] B,
  output Zero_Bit,
  output [31:0] Alu_Output
);

  wire comparator_1_lt;
  wire [31:0] adder_1_out, and_1_out, bit_extender_1_out, or_1_out, subtractor_1_out;

  assign and_1_out = B & B;  // AND_Gate and_1, 32 bits wide
  assign or_1_out = A | B;  // OR_Gate or_1, 32 bits wide
  Adder #(.width(32)) adder_1 (.a(B), .b(A), .out(adder_1_out));  // open: cin, cout
  Subtractor #(.width(32)) subtractor_1 (.a(B), .b(A), .out(subtractor_1_out));  // open: bin, bout
  Comparator #(.width(32), .mode("unsigned")) comparator_1 (.a(A), .b(B), .lt(comparator_1_lt));  // open: gt, eq
  assign bit_extender_1_out = {{31{1'b0}}, comparator_1_lt};  // Bit_Extender bit_extender_1
  Multiplexer #(.select(3), .width(32)) multiplexer_1 (
    .in0(and_1_out), .in1(or_1_out), .in2(adder_1_out), .in6(subtractor_1_out), .in7(bit_extender_1_out),
    .out(Alu_Output), .sel(S0S1S2));  // open: in3, in4, in5, en
  Comparator #(.width(32)) comparator_2 (.a({32{1'b0}}), .b(Alu_Output), .eq(Zero_Bit));  // open: gt, lt

  // Notes on the sheet:
  //   Inputs
  //   Output
endmodule

module RegFile (
  input  [4:0] Read_0,
  input  [4:0] Read_1,
  input  RegWrite,
  input  clear,
  input  [31:0] write_value,
  input  [4:0] write_addr,
  input  clock,
  output [31:0] v0,
  output [31:0] Value_0,
  output [31:0] Value_1
);

  wire decoder_1_out1, decoder_1_out2, decoder_1_out3, decoder_1_out4, decoder_1_out5, decoder_1_out6,
       decoder_1_out7, decoder_1_out8, decoder_1_out9, decoder_1_out10, decoder_1_out11, decoder_1_out12,
       decoder_1_out13, decoder_1_out14, decoder_1_out15, decoder_1_out16, decoder_1_out17, decoder_1_out18,
       decoder_1_out19, decoder_1_out20, decoder_1_out21, decoder_1_out22, decoder_1_out23, decoder_1_out24,
       decoder_1_out25, decoder_1_out26, decoder_1_out27, decoder_1_out28, decoder_1_out29, decoder_1_out30,
       decoder_1_out31;
  wire [31:0] a0_q, a1_q, a2_q, a3_q, at_q, fp_q, gp_q, k0_q, k1_q, ra_q, s0_q, s1_q, s2_q, s3_q, s4_q, s5_q,
       s6_q, s7_q, sp_q, t0_q, t1_q, t2_q, t3_q, t4_q, t5_q, t6_q, t7_q, t8_q, t9_q, v1_q;

  Decoder #(.select(5)) decoder_1 (
    .out1(decoder_1_out1), .out2(decoder_1_out2), .out3(decoder_1_out3), .out4(decoder_1_out4),
    .out5(decoder_1_out5), .out6(decoder_1_out6), .out7(decoder_1_out7), .out8(decoder_1_out8),
    .out9(decoder_1_out9), .out10(decoder_1_out10), .out11(decoder_1_out11), .out12(decoder_1_out12),
    .out13(decoder_1_out13), .out14(decoder_1_out14), .out15(decoder_1_out15), .out16(decoder_1_out16),
    .out17(decoder_1_out17), .out18(decoder_1_out18), .out19(decoder_1_out19), .out20(decoder_1_out20),
    .out21(decoder_1_out21), .out22(decoder_1_out22), .out23(decoder_1_out23), .out24(decoder_1_out24),
    .out25(decoder_1_out25), .out26(decoder_1_out26), .out27(decoder_1_out27), .out28(decoder_1_out28),
    .out29(decoder_1_out29), .out30(decoder_1_out30), .out31(decoder_1_out31), .sel(write_addr), .en(RegWrite));  // open: out0
  Register #(.width(32)) at (.D(write_value), .en(decoder_1_out1), .Q(at_q), .clk(clock), .clr(clear));
  Register #(.width(32)) u_v0 (.D(write_value), .en(decoder_1_out2), .Q(v0), .clk(clock), .clr(clear));
  Register #(.width(32)) v1 (.D(write_value), .en(decoder_1_out3), .Q(v1_q), .clk(clock), .clr(clear));
  Register #(.width(32)) a0 (.D(write_value), .en(decoder_1_out4), .Q(a0_q), .clk(clock), .clr(clear));
  Register #(.width(32)) a1 (.D(write_value), .en(decoder_1_out5), .Q(a1_q), .clk(clock), .clr(clear));
  Register #(.width(32)) a2 (.D(write_value), .en(decoder_1_out6), .Q(a2_q), .clk(clock), .clr(clear));
  Register #(.width(32)) a3 (.D(write_value), .en(decoder_1_out7), .Q(a3_q), .clk(clock), .clr(clear));
  Register #(.width(32)) t0 (.D(write_value), .en(decoder_1_out8), .Q(t0_q), .clk(clock), .clr(clear));
  Register #(.width(32)) t1 (.D(write_value), .en(decoder_1_out9), .Q(t1_q), .clk(clock), .clr(clear));
  Register #(.width(32)) t2 (.D(write_value), .en(decoder_1_out10), .Q(t2_q), .clk(clock), .clr(clear));
  Register #(.width(32)) t3 (.D(write_value), .en(decoder_1_out11), .Q(t3_q), .clk(clock), .clr(clear));
  Register #(.width(32)) t4 (.D(write_value), .en(decoder_1_out12), .Q(t4_q), .clk(clock), .clr(clear));
  Register #(.width(32)) t5 (.D(write_value), .en(decoder_1_out13), .Q(t5_q), .clk(clock), .clr(clear));
  Register #(.width(32)) t6 (.D(write_value), .en(decoder_1_out14), .Q(t6_q), .clk(clock), .clr(clear));
  Register #(.width(32)) t7 (.D(write_value), .en(decoder_1_out15), .Q(t7_q), .clk(clock), .clr(clear));
  Register #(.width(32)) s0 (.D(write_value), .en(decoder_1_out16), .Q(s0_q), .clk(clock), .clr(clear));
  Register #(.width(32)) s1 (.D(write_value), .en(decoder_1_out17), .Q(s1_q), .clk(clock), .clr(clear));
  Register #(.width(32)) s2 (.D(write_value), .en(decoder_1_out18), .Q(s2_q), .clk(clock), .clr(clear));
  Register #(.width(32)) s3 (.D(write_value), .en(decoder_1_out19), .Q(s3_q), .clk(clock), .clr(clear));
  Register #(.width(32)) s4 (.D(write_value), .en(decoder_1_out20), .Q(s4_q), .clk(clock), .clr(clear));
  Register #(.width(32)) s5 (.D(write_value), .en(decoder_1_out21), .Q(s5_q), .clk(clock), .clr(clear));
  Register #(.width(32)) s6 (.D(write_value), .en(decoder_1_out22), .Q(s6_q), .clk(clock), .clr(clear));
  Register #(.width(32)) s7 (.D(write_value), .en(decoder_1_out23), .Q(s7_q), .clk(clock), .clr(clear));
  Register #(.width(32)) t8 (.D(write_value), .en(decoder_1_out24), .Q(t8_q), .clk(clock), .clr(clear));
  Register #(.width(32)) t9 (.D(write_value), .en(decoder_1_out25), .Q(t9_q), .clk(clock), .clr(clear));
  Register #(.width(32)) k0 (.D(write_value), .en(decoder_1_out26), .Q(k0_q), .clk(clock), .clr(clear));
  Register #(.width(32)) k1 (.D(write_value), .en(decoder_1_out27), .Q(k1_q), .clk(clock), .clr(clear));
  Register #(.width(32)) gp (.D(write_value), .en(decoder_1_out28), .Q(gp_q), .clk(clock), .clr(clear));
  Register #(.width(32)) sp (.D(write_value), .en(decoder_1_out29), .Q(sp_q), .clk(clock), .clr(clear));
  Register #(.width(32)) fp (.D(write_value), .en(decoder_1_out30), .Q(fp_q), .clk(clock), .clr(clear));
  Register #(.width(32)) ra (.D(write_value), .en(decoder_1_out31), .Q(ra_q), .clk(clock), .clr(clear));
  Multiplexer #(.select(5), .width(32)) multiplexer_1 (
    .in0({32{1'b0}}), .in1(at_q), .in2(v0), .in3(v1_q), .in4(a0_q), .in5(a1_q), .in6(a2_q), .in7(a3_q),
    .in8(t0_q), .in9(t1_q), .in10(t2_q), .in11(t3_q), .in12(t4_q), .in13(t5_q), .in14(t6_q), .in15(t7_q),
    .in16(s0_q), .in17(s1_q), .in18(s2_q), .in19(s3_q), .in20(s4_q), .in21(s5_q), .in22(s6_q), .in23(s7_q),
    .in24(t8_q), .in25(t9_q), .in26(k0_q), .in27(k1_q), .in28(gp_q), .in29(sp_q), .in30(fp_q), .in31(ra_q),
    .out(Value_0), .sel(Read_0));  // open: en
  Multiplexer #(.select(5), .width(32)) multiplexer_2 (
    .in0({32{1'b0}}), .in1(at_q), .in2(v0), .in3(v1_q), .in4(a0_q), .in5(a1_q), .in6(a2_q), .in7(a3_q),
    .in8(t0_q), .in9(t1_q), .in10(t2_q), .in11(t3_q), .in12(t4_q), .in13(t5_q), .in14(t6_q), .in15(t7_q),
    .in16(s0_q), .in17(s1_q), .in18(s2_q), .in19(s3_q), .in20(s4_q), .in21(s5_q), .in22(s6_q), .in23(s7_q),
    .in24(t8_q), .in25(t9_q), .in26(k0_q), .in27(k1_q), .in28(gp_q), .in29(sp_q), .in30(fp_q), .in31(ra_q),
    .out(Value_1), .sel(Read_1));  // open: en
endmodule

module Reg_Splitter (
  input  [31:0] in_1,
  output [25:0] _0_25,
  output [4:0] _21_25,
  output [4:0] _16_20,
  output [4:0] _11_15,
  output [5:0] _26_31,
  output [5:0] _0_5,
  output [15:0] _0_15
);


  assign _0_5 = in_1[5:0];
  assign _0_15 = in_1[15:0];
  assign _0_25 = in_1[25:0];
  assign _11_15 = in_1[15:11];
  assign _16_20 = in_1[20:16];
  assign _21_25 = in_1[25:21];
  assign _26_31 = in_1[31:26];
endmodule

module ALUControl (
  input  [5:0] OpCode,
  input  [5:0] Funct,
  output REGWRT,
  output MEMTOREG,
  output MEMWRITE,
  output BRANCH,
  output [2:0] ALU_Control,
  output ALUSRC,
  output REGDST
);

  wire not_1_out, not_2_out, not_4_out, not_5_out;
  wire [1:0] or_1_out;
  wire [1:1] and_2_out;

  not not_1 (not_1_out, OpCode[3]);
  not not_2 (not_2_out, OpCode[2]);
  not not_3 (REGDST, OpCode[1]);
  not not_4 (not_4_out, OpCode[2]);
  not not_5 (not_5_out, OpCode[1]);
  and and_1 (REGWRT, not_1_out, not_2_out);
  and and_2 (and_2_out[1], not_4_out, not_5_out);
  not not_6 (or_1_out[1], Funct[2]);
  or or_1 (or_1_out[0], Funct[0], Funct[3]);
  Multiplexer #(.select(2), .width(3), .enable("false")) multiplexer_1 (
    .in0(3'b010), .in1(3'b110), .in2({Funct[1], or_1_out}), .in3({Funct[1], or_1_out}), .out(ALU_Control),
    .sel({and_2_out[1], OpCode[2]}));

  assign ALUSRC = OpCode[1];
  assign BRANCH = OpCode[2];
  assign MEMTOREG = OpCode[1];
  assign MEMWRITE = OpCode[3];
endmodule
