// Logisim project Test.circ as structural Verilog: 7 circuits, main circuit main
module main (
);

  wire alu_cont_1_p1, and_1_out, clock_1_out, Control_Unit_p1, Control_Unit_p3, Control_Unit_p4,
       Control_Unit_p5, Control_Unit_p7, Control_Unit_p8, Control_Unit_p9, main_1_p3, main_1_p4,
       n32_register_file_1_p5, n32_register_file_1_p6, not_1_out, or_1_out, Splitter_p2, Splitter_p3,
       Splitter_p5;
  wire [3:0] PC_31_28_out_2;
  wire [4:0] multiplexer_1_out, Splitter_p6, Splitter_p7;
  wire [15:0] Splitter_p8;
  wire [23:0] S_J_2_out_2, S_J_out_2, shifter_1_out, shifter_4_out;
  wire [25:0] Splitter_p4;
  wire [27:0] bit_extender_1_out, shifter_2_out;
  wire [31:0] adder_1_out, adder_2_out, bit_extender_2_out, INS_28_0__PC_31_28_out_3, main_1_p5,
       multiplexer_2_out, multiplexer_3_out, multiplexer_4_out, n32_register_file_1_p4,
       n32_register_file_1_p7, PC_q, ram_1_data, rom_1_data, shifter_3_out;

  Clock clock_1 (.out(clock_1_out));
  Splitter_for_Mems S_J (.in_1(PC_q), .out_2(S_J_out_2));
  Register #(.width(32)) PC (.D(multiplexer_4_out), .Q(PC_q), .clk(clock_1_out));  // open: en, clr
  Adder #(.width(32)) adder_1 (.a(PC_q), .b(32'h4), .out(adder_1_out));  // open: cin, cout
  Shifter #(.width(24), .shift("lr")) shifter_1 (.in(S_J_out_2), .\dist (5'b00010), .out(shifter_1_out));
  ROM #(.addrWidth(24), .dataWidth(32)) rom_1 (.addr(shifter_1_out), .data(rom_1_data));  // open: sel
  assign bit_extender_1_out = {{2{Splitter_p4[25]}}, Splitter_p4};  // Bit_Extender bit_extender_1
  // Splitter_Reg Splitter: pin names not known; wires that end beside it: rom_1_data, Splitter_p2, Splitter_p3, Splitter_p4, Splitter_p5, Splitter_p6, Splitter_p7, Splitter_p8
  Shifter #(.width(28)) shifter_2 (.in(bit_extender_1_out), .\dist (5'b00010), .out(shifter_2_out));
  Multiplexer #(.width(5), .enable("false")) multiplexer_1 (
    .in0(Splitter_p6), .in1(Splitter_p7), .out(multiplexer_1_out), .sel(Control_Unit_p1));
  Spliier_PC PC_31_28 (.in_1(adder_1_out), .out_2(PC_31_28_out_2));
  Shifter #(.width(32)) shifter_3 (.in(bit_extender_2_out), .\dist (5'b00010), .out(shifter_3_out));
  // _32_register_file 32_register_file_1: pin names not known; wires that end beside it: Splitter_p5, Splitter_p6, multiplexer_1_out, n32_register_file_1_p4, n32_register_file_1_p5, n32_register_file_1_p6, n32_register_file_1_p7
  assign bit_extender_2_out = {{16{Splitter_p8[15]}}, Splitter_p8};  // Bit_Extender bit_extender_2
  Join_PC INS_28_0__PC_31_28 (.in_1(shifter_2_out), .in_2(PC_31_28_out_2), .out_3(INS_28_0__PC_31_28_out_3));
  Multiplexer #(.width(32), .enable("false")) multiplexer_2 (
    .in0(n32_register_file_1_p7), .in1(bit_extender_2_out), .out(multiplexer_2_out), .sel(Control_Unit_p3));
  Multiplexer #(.width(32), .enable("false")) multiplexer_3 (
    .in0(adder_1_out), .in1(adder_2_out), .out(multiplexer_3_out), .sel(and_1_out));
  Adder #(.width(32)) adder_2 (.a(adder_1_out), .b(shifter_3_out), .out(adder_2_out));  // open: cin, cout
  and and_1 (and_1_out, main_1_p4, Control_Unit_p8);
  // ALU__main main_1: pin names not known; wires that end beside it: n32_register_file_1_p6, multiplexer_2_out, main_1_p3, main_1_p4, main_1_p5
  // ALU_Cont alu_cont_1: pin names not known; wires that end beside it: alu_cont_1_p1, Splitter_p2, alu_cont_1_p1, main_1_p3
  Multiplexer #(.width(32), .enable("false")) multiplexer_4 (
    .in0(INS_28_0__PC_31_28_out_3), .in1(multiplexer_3_out), .out(multiplexer_4_out), .sel(not_1_out));
  not not_1 (not_1_out, Control_Unit_p9);
  Splitter_for_Mems S_J_2 (.in_1(main_1_p5), .out_2(S_J_2_out_2));
  // Control_Unit Control_Unit: pin names not known; wires that end beside it: Control_Unit_p1, n32_register_file_1_p5, Control_Unit_p3, Control_Unit_p4, Control_Unit_p5, Splitter_p3, Control_Unit_p7, Control_Unit_p8, Control_Unit_p9, alu_cont_1_p1
  Shifter #(.width(24), .shift("lr")) shifter_4 (.in(S_J_2_out_2), .\dist (5'b00010), .out(shifter_4_out));
  or or_1 (or_1_out, Control_Unit_p4, Control_Unit_p5);
  RAM #(.addrWidth(24), .dataWidth(32), .bus("separate")) ram_1 (
    .addr(shifter_4_out), .din(n32_register_file_1_p7), .data(ram_1_data), .str(Control_Unit_p4),
    .sel(or_1_out), .clk(clock_1_out), .ld(Control_Unit_p5));  // open: clr
  Multiplexer #(.width(32), .enable("false")) multiplexer_5 (
    .in0(ram_1_data), .in1(main_1_p5), .out(n32_register_file_1_p4), .sel(Control_Unit_p7));

  // Notes on the sheet:
  //   IM
  //   contents of rom_1 (hex, n*v repeats v):
  //   0 8c010000 8c020004 221820 ac030008 8000000
  //   Rdst
  //   RF
  //   ASrc
  //   PSrc
  //   JMP
  //   ALU
  //   M2R
endmodule

module Splitter_Reg (
  input  [31:0] IM,
  output [25:0] out_2,
  output [4:0] a1,
  output [4:0] a2,
  output [4:0] to_mux_ctrl_regdst,
  output [5:0] opcode,
  output [5:0] \function ,
  output [15:0] to_sign_extension
);


  assign a1 = IM[25:21];
  assign a2 = IM[20:16];
  assign \function  = IM[5:0];
  assign opcode = IM[31:26];
  assign out_2 = IM[25:0];
  assign to_mux_ctrl_regdst = IM[15:11];
  assign to_sign_extension = IM[15:0];
endmodule

module Spliier_PC (
  input  [31:0] in_1,
  output [3:0] out_2
);


  assign out_2 = in_1[31:28];
endmodule

module Join_PC (
  input  [27:0] in_1,
  input  [3:0] in_2,
  output [31:0] out_3
);


  assign out_3 = {in_2, in_1};
endmodule

module Splitter_for_Mems (
  input  [31:0] in_1,
  output [23:0] out_2
);


  assign out_2 = in_1[23:0];
endmodule

module Control_Unit (
  input  op5,
  input  op4,
  input  op3,
  input  op2,
  input  op1,
  input  op0,
  output RDST1,
  output RDST0,
  output RW,
  output ASRC,
  output MW,
  output MR,
  output M2R,
  output BRN,
  output JMP,
  output aluop1,
  output aluop0
);

  wire and_3_out, and_4_out, not_1_out, not_2_out, not_3_out, not_4_out, not_5_out, not_6_out, not_7_out,
       not_8_out, not_9_out, not_10_out;

  not not_1 (not_1_out, op3);
  not not_2 (not_2_out, op1);
  not not_3 (not_3_out, op2);
  not not_4 (not_4_out, op1);
  not not_5 (not_5_out, op3);
  or or_1 (ASRC, op1, op3);
  and and_1 (MW, op5, op3);
  not not_6 (not_6_out, op3);
  not not_7 (not_7_out, op0);
  not not_8 (not_8_out, op3);
  not not_9 (not_9_out, op2);
  not not_10 (not_10_out, op1);
  and and_2 (RDST1, not_1_out, not_2_out);
  and and_3 (and_3_out, not_3_out, not_4_out);
  or or_2 (RW, and_3_out, and_4_out);
  and and_4 (and_4_out, op5, not_5_out);
  and and_5 (MR, op5, not_6_out);
  and and_6 (JMP, op1, not_7_out);
  and and_7 (aluop1, not_8_out, not_9_out, not_10_out);

  assign aluop0 = op2;
  assign BRN = op2;
  assign M2R = op1;
endmodule

module ALU_Cont (
  input  AluOp0,
  input  AluIp1,
  input  _5,
  input  _4,
  input  _3,
  input  _2,
  input  _1,
  input  _0,
  output _2_2,
  output _1_2,
  output _0_2
);

  wire and_1_out, and_2_out, and_3_out, not_1_out, not_2_out, not_3_out, not_4_out;

  and and_1 (and_1_out, AluIp1, _1);
  not not_1 (not_1_out, AluIp1);
  not not_2 (not_2_out, _2);
  not not_3 (not_3_out, AluOp0);
  not not_4 (not_4_out, AluOp0);
  or or_1 (_2_2, AluOp0, and_1_out);
  or or_2 (_1_2, not_1_out, not_2_out, AluOp0);
  and and_2 (and_2_out, AluIp1, not_3_out, _0);
  or or_3 (_0_2, and_2_out, and_3_out);
  and and_3 (and_3_out, AluIp1, not_4_out, _3);
endmodule
