// Logisim project alu control.circ as structural Verilog
module Alu_Control (
  input  OPC1,
  input  OPC0,
  input  FUN5,
  input  FUN4,
  input  FUN3,
  input  FUN2,
  input  FUN1,
  input  FUN0,
  output ALUOP2,
  output ALUOP1,
  output ALUOP0
);

  wire and_1_out, and_2_out, and_3_out, and_4_out, not_1_out, not_2_out, not_3_out;

  and and_1 (and_1_out, OPC1, not_1_out);
  not not_1 (not_1_out, FUN5);
  and and_2 (and_2_out, OPC1, FUN1);
  not not_2 (not_2_out, OPC1);
  or or_1 (ALUOP1, not_2_out, not_3_out);
  not not_3 (not_3_out, FUN2);
  and and_3 (and_3_out, OPC1, FUN0);
  and and_4 (and_4_out, OPC1, FUN3);
  or or_2 (ALUOP2, OPC0, and_1_out, and_2_out);
  or or_3 (ALUOP0, and_3_out, and_4_out);
endmodule

module Alu (
  input  OPC1,
  input  OPC0,
  input  FUN5,
  input  FUN4,
  input  FUN3,
  input  FUN2,
  input  FUN1,
  input  FUN0,
  output ALUOP2,
  output ALUOP1,
  output ALUOP0
);

  wire and_1_out, and_2_out, and_3_out, and_4_out, not_1_out, not_2_out, not_3_out;

  and and_1 (and_1_out, OPC1, not_1_out);
  not not_1 (not_1_out, FUN5);
  and and_2 (and_2_out, OPC1, FUN1);
  not not_2 (not_2_out, OPC1);
  or or_1 (ALUOP1, not_2_out, not_3_out);
  not not_3 (not_3_out, FUN2);
  and and_3 (and_3_out, OPC1, FUN0);
  and and_4 (and_4_out, OPC1, FUN3);
  or or_2 (ALUOP2, OPC0, and_1_out, and_2_out);
  or or_3 (ALUOP0, and_3_out, and_4_out);
endmodule
