// Logisim project control2.circ as structural Verilog: 3 circuits, main circuit main
module main (
);

  wire [7:0] multiplexer_1_out;

  Multiplexer #(.select(5), .width(8)) multiplexer_1 (.out(multiplexer_1_out));  // open: in0, in1, in2, in3, in4, in5, in6, in7, in8, in9, in10, in11, in12, in13, in14, in15, in16, in17, in18, in19, in20, in21, in22, in23, in24, in25, in26, in27, in28, in29, in30, in31, sel, en
endmodule

module Control (
  input  op5,
  input  op4,
  input  op3,
  input  op2,
  input  op1,
  input  op0,
  output RDST,
  output RW,
  output ASRC,
  output MW,
  output MR,
  output M2R,
  output BRN,
  output JMP
);

  wire and_1_out, and_2_out, not_2_out, not_3_out, not_4_out, not_5_out, not_6_out;

  not not_1 (RDST, op1);
  not not_2 (not_2_out, op2);
  not not_3 (not_3_out, op1);
  not not_4 (not_4_out, op3);
  not not_5 (not_5_out, op3);
  not not_6 (not_6_out, op0);
  and and_1 (and_1_out, not_2_out, not_3_out);
  and and_2 (and_2_out, op5, not_4_out);
  and and_3 (MR, op5, not_5_out);
  and and_4 (JMP, op1, not_6_out);
  or or_1 (RW, and_1_out, and_2_out);

  assign ASRC = op1;
  assign BRN = op2;
  assign M2R = op1;
  assign MW = op3;
endmodule

module control2 (
  input  op5,
  input  op4,
  input  op3,
  input  op2,
  input  op1,
  input  op0,
  output RDST,
  output RW,
  output ASRC,
  output MW,
  output MR,
  output M2R,
  output BRN,
  output JMP,
  output ALUOP1,
  output ALUOP0
);

  wire and_3_out, and_4_out, not_1_out, not_2_out, not_3_out, not_4_out, not_5_out, not_6_out, not_7_out,
       not_8_out, not_9_out, not_10_out;

  not not_1 (not_1_out, op3);
  not not_2 (not_2_out, op1);
  not not_3 (not_3_out, op2);
  not not_4 (not_4_out, op1);
  not not_5 (not_5_out, op3);
  or or_1 (ASRC, op1, op3);
  and and_1 (MW, op5, op3);
  not not_6 (not_6_out, op3);
  not not_7 (not_7_out, op0);
  not not_8 (not_8_out, op3);
  not not_9 (not_9_out, op2);
  not not_10 (not_10_out, op1);
  and and_2 (RDST, not_1_out, not_2_out);
  and and_3 (and_3_out, not_3_out, not_4_out);
  and and_4 (and_4_out, op5, not_5_out);
  and and_5 (MR, op5, not_6_out);
  and and_6 (JMP, op1, not_7_out);
  and and_7 (ALUOP1, not_8_out, not_9_out, not_10_out);
  or or_2 (RW, and_3_out, and_4_out);

  assign ALUOP0 = op2;
  assign BRN = op2;
  assign M2R = op1;
endmodule
