// Logisim project lab9ques.circ as structural Verilog: 2 circuits, main circuit main
module main (
  input  [1:0] OP0,
  input  [5:0] func,
  output [2:0] out_3
);

  wire and_1_out, and_2_out, and_3_out, not_1_out, not_2_out, not_3_out, not_4_out;

  and and_1 (and_1_out, OP0[1], func[1]);
  not not_1 (not_1_out, OP0[1]);
  not not_2 (not_2_out, func[2]);
  not not_3 (not_3_out, OP0[0]);
  not not_4 (not_4_out, OP0[0]);
  or or_1 (out_3[2], OP0[0], and_1_out);
  or or_2 (out_3[1], not_1_out, not_2_out, OP0[0]);
  and and_2 (and_2_out, OP0[1], not_3_out, func[0]);
  or or_3 (out_3[0], and_2_out, and_3_out);
  and and_3 (and_3_out, OP0[1], not_4_out, func[3]);
endmodule

module CONTROL_UNIT (
  input  [1:0] OP0,
  input  [5:0] func,
  output [2:0] out_3
);

  wire and_1_out, and_2_out, and_3_out, not_1_out, not_2_out, not_3_out, not_4_out;

  and and_1 (and_1_out, OP0[1], func[1]);
  not not_1 (not_1_out, OP0[1]);
  not not_2 (not_2_out, func[2]);
  not not_3 (not_3_out, OP0[0]);
  not not_4 (not_4_out, OP0[0]);
  or or_1 (out_3[2], OP0[0], and_1_out);
  or or_2 (out_3[1], not_1_out, not_2_out, OP0[0]);
  and and_2 (and_2_out, OP0[1], not_3_out, func[0]);
  or or_3 (out_3[0], and_2_out, and_3_out);
  and and_3 (and_3_out, OP0[1], not_4_out, func[3]);
endmodule
