// Logisim project ques2_lab10.circ as structural Verilog: 1 circuit, main circuit main
module main (
);

  wire undriven_2;
  wire [31:0] multiplexer_1_out, PC_q, undriven;

  Multiplexer #(.width(32)) multiplexer_1 (.in1(undriven), .out(multiplexer_1_out), .sel(undriven_2));  // open: in0, en
  Register #(.width(32)) PC (.D(multiplexer_1_out), .Q(PC_q));  // open: en, clk, clr
endmodule
