// Logisim project architecture.circ as structural Verilog: 5 circuits, main circuit main
module main (
);

  wire ALU_p3, ALU_p5, n32_register_file_1_p5;
  wire [3:0] PC_31_28_out_2;
  wire [4:0] multiplexer_1_out, Splitter_out_3, Splitter_out_4, Splitter_out_5;
  wire [15:0] Splitter_out_8;
  wire [23:0] S_J_2_out_2, S_J_out_2;
  wire [25:0] Splitter_out_2;
  wire [27:0] bit_extender_1_out, shifter_1_out;
  wire [31:0] adder_1_out, adder_2_out, ALU_p6, bit_extender_2_out, INS_28_0__PC_31_28_out_3,
       multiplexer_2_out, multiplexer_3_out, multiplexer_4_out, n32_register_file_1_p4,
       n32_register_file_1_p6, PC_q, ram_1_data, rom_1_data, shifter_2_out;

  Splitter_for_Mems S_J (.in_1(PC_q), .out_2(S_J_out_2));
  Register #(.width(32)) PC (.D(multiplexer_4_out), .Q(PC_q));  // open: en, clk, clr
  Adder #(.width(32)) adder_1 (.a(PC_q), .b(32'h4), .out(adder_1_out));  // open: cin, cout
  ROM #(.addrWidth(24), .dataWidth(32)) rom_1 (.addr(S_J_out_2), .data(rom_1_data));  // open: sel
  assign bit_extender_1_out = {{2{Splitter_out_2[25]}}, Splitter_out_2};  // Bit_Extender bit_extender_1
  Splitter_Reg Splitter (
    .in_1(rom_1_data), .out_2(Splitter_out_2), .out_3(Splitter_out_3), .out_4(Splitter_out_4),
    .out_5(Splitter_out_5), .out_8(Splitter_out_8));  // open: out_7, out_6
  Shifter #(.width(28)) shifter_1 (.in(bit_extender_1_out), .\dist (5'b00010), .out(shifter_1_out));
  Multiplexer #(.width(5), .enable("false")) multiplexer_1 (
    .in0(Splitter_out_4), .in1(Splitter_out_5), .out(multiplexer_1_out));  // open: sel
  Spliier_PC PC_31_28 (.in_1(adder_1_out), .out_2(PC_31_28_out_2));
  Shifter #(.width(32)) shifter_2 (.in(bit_extender_2_out), .\dist (5'b00010), .out(shifter_2_out));
  // _32_register_file 32_register_file_1: pin names not known; wires that end beside it: Splitter_out_3, Splitter_out_4, multiplexer_1_out, n32_register_file_1_p4, n32_register_file_1_p5, n32_register_file_1_p6
  assign bit_extender_2_out = {{16{Splitter_out_8[15]}}, Splitter_out_8};  // Bit_Extender bit_extender_2
  Join_PC INS_28_0__PC_31_28 (.in_1(shifter_1_out), .in_2(PC_31_28_out_2), .out_3(INS_28_0__PC_31_28_out_3));
  Multiplexer #(.width(32), .enable("false")) multiplexer_2 (
    .in0(n32_register_file_1_p6), .in1(bit_extender_2_out), .out(multiplexer_2_out));  // open: sel
  Multiplexer #(.width(32), .enable("false")) multiplexer_3 (
    .in0(adder_1_out), .in1(adder_2_out), .out(multiplexer_3_out));  // open: sel
  Adder #(.width(32)) adder_2 (.a(adder_1_out), .b(shifter_2_out), .out(adder_2_out));  // open: cin, cout
  // ALU ALU: pin names not known; wires that end beside it: n32_register_file_1_p5, multiplexer_2_out, ALU_p3, ALU_p3, ALU_p5, ALU_p6, ALU_p5
  Multiplexer #(.width(32), .enable("false")) multiplexer_4 (
    .in0(INS_28_0__PC_31_28_out_3), .in1(multiplexer_3_out), .out(multiplexer_4_out));  // open: sel
  Splitter_for_Mems S_J_2 (.in_1(ALU_p6), .out_2(S_J_2_out_2));
  RAM #(.addrWidth(24), .dataWidth(32), .bus("separate")) ram_1 (
    .addr(S_J_2_out_2), .din(n32_register_file_1_p6), .data(ram_1_data));  // open: str, sel, clk, ld, clr
  Multiplexer #(.width(32), .enable("false")) multiplexer_5 (
    .in0(ram_1_data), .in1(ALU_p6), .out(n32_register_file_1_p4));  // open: sel

  // Notes on the sheet:
  //   IM
  //   Rdst
  //   RF
  //   ASrc
  //   PSrc
  //   JMP
  //   ALU
  //   M2R
endmodule

module Splitter_Reg (
  input  [31:0] in_1,
  output [25:0] out_2,
  output [4:0] out_3,
  output [4:0] out_4,
  output [4:0] out_5,
  output [5:0] out_6,
  output [5:0] out_7,
  output [15:0] out_8
);


  assign out_2 = in_1[25:0];
  assign out_3 = in_1[25:21];
  assign out_4 = in_1[20:16];
  assign out_5 = in_1[15:11];
  assign out_6 = in_1[31:26];
  assign out_7 = in_1[5:0];
  assign out_8 = in_1[15:0];
endmodule

module Spliier_PC (
  input  [31:0] in_1,
  output [3:0] out_2
);


  assign out_2 = in_1[31:28];
endmodule

module Join_PC (
  input  [27:0] in_1,
  input  [3:0] in_2,
  output [31:0] out_3
);


  assign out_3 = {in_2, in_1};
endmodule

module Splitter_for_Mems (
  input  [31:0] in_1,
  output [23:0] out_2
);


  assign out_2 = in_1[23:0];
endmodule
